// Logisim project Project1.circ as structural Verilog: 11 circuits, main circuit Main
module Main (
  input  reset
);

  wire clk, Controller_alusrc, Controller_memwrite, Controller_npc_sel, Controller_pc_j, Controller_regdst,
       Controller_regwrite, jal_sel, Mem2Reg, zero;
  wire [1:0] Controller_extop;
  wire [2:0] Controller_aluctr;
  wire [4:0] multiplexer_1_out;
  wire [5:0] opcode;
  wire [25:0] addr;
  wire [31:0] ALU_out, DM_dmout, Extender_extimm32, GPR_rd1, GPR_rd2, multiplexer_2_out, multiplexer_3_out,
       multiplexer_4_out, pc_4;

  Clock u_clk (.out(clk));
  IFU IFU (
    .instr({opcode, addr}), .nPC_sel(Controller_npc_sel), .zero(zero), .clk(clk), .reset(reset),
    .PC_j(Controller_pc_j), .pc_4(pc_4));
  // Probe on {opcode, addr}
  // Probe on opcode
  // Probe on addr[5:0]
  Controller Controller (
    .RegDst(Controller_regdst), .ALUSrc(Controller_alusrc), .MemtoReg(Mem2Reg),
    .RegWrite(Controller_regwrite), .MemWrite(Controller_memwrite), .nPC_sel(Controller_npc_sel),
    .ExtOp(Controller_extop), .ALUCtr(Controller_aluctr), .opcode(opcode), .funct(addr[5:0]),
    .PC_j(Controller_pc_j), .jal_sel(jal_sel));
  GPR GPR (
    .WE_regwrite(Controller_regwrite), .clk(clk), .RD1(GPR_rd1), .RD2(GPR_rd2), .WD(multiplexer_2_out),
    .RA(addr[25:21]), .RB(addr[20:16]), .RW(multiplexer_1_out), .reset(reset), .jal_sel(jal_sel));
  Multiplexer #(.width(5), .disabled(0), .enable("false")) multiplexer_1 (
    .in0(addr[20:16]), .in1(addr[15:11]), .out(multiplexer_1_out), .sel(Controller_regdst));
  Multiplexer #(.width(32), .enable("false")) multiplexer_2 (
    .in0(multiplexer_3_out), .in1(pc_4), .out(multiplexer_2_out), .sel(jal_sel));
  Extender Extender (.Imm16(addr[15:0]), .Extsel(Controller_extop), .ExtImm32(Extender_extimm32));
  Multiplexer #(.width(32), .enable("false")) multiplexer_3 (
    .in0(ALU_out), .in1(DM_dmout), .out(multiplexer_3_out), .sel(Mem2Reg));
  Multiplexer #(.width(32), .enable("false")) multiplexer_4 (
    .in0(GPR_rd2), .in1(Extender_extimm32), .out(multiplexer_4_out), .sel(Controller_alusrc));
  ALU ALU (.A(GPR_rd1), .B(multiplexer_4_out), .out(ALU_out), .F(Controller_aluctr), .zero(zero));
  DM DM (
    .A(ALU_out[4:0]), .D(GPR_rd2), .MemWrite(Controller_memwrite), .dmout(DM_dmout), .reset(reset),
    .MemtoReg(Mem2Reg), .clk(clk));

  // Other names for the same wires on the sheet: funct[5:0] = addr[5:0]; imm[15:0] = addr[15:0];
  //   shamt[4:0] = addr[10:6]; rd[4:0] = addr[15:11]; rt[4:0] = addr[20:16]; rs[4:0] = addr[25:21]
endmodule

module IFU (
  input  clk,
  input  reset,
  input  PC_j,
  input  nPC_sel,
  input  zero,
  output [31:0] pc_4,
  output [31:0] instr
);

  wire and_1_out;
  wire [29:0] adder_2_out, bit_extender_1_out, multiplexer_1_out, multiplexer_2_out, pc, pc_q;

  Register #(.width(30)) u_pc (.D(multiplexer_2_out), .en(1'b1), .Q(pc_q), .clk(clk), .clr(reset));
  Adder #(.width(30)) adder_1 (.a(pc_q), .b(30'h1), .out(pc));  // open: cin, cout
  assign bit_extender_1_out = {{14{instr[15]}}, instr[15:0]};  // Bit_Extender bit_extender_1
  assign pc_4 = {{2{1'b0}}, pc};  // Bit_Extender bit_extender_2
  Multiplexer #(.width(30), .enable("false")) multiplexer_1 (
    .in0(pc), .in1(adder_2_out), .out(multiplexer_1_out), .sel(and_1_out));
  Adder #(.width(30)) adder_2 (.a(pc), .b(bit_extender_1_out), .out(adder_2_out));  // open: cin, cout
  and and_1 (and_1_out, nPC_sel, zero);
  ROM #(.addrWidth(5), .dataWidth(32)) rom_1 (.addr(pc_q[4:0]), .data(instr));  // open: sel
  Multiplexer #(.width(30), .enable("false")) multiplexer_2 (
    .in0(multiplexer_1_out), .in1({pc[29:26], instr[25:0]}), .out(multiplexer_2_out), .sel(PC_j));

  // Notes on the sheet:
  //   contents of rom_1 (hex, n*v repeats v):
  //   34030023 34060043 664021 c34823 ad290000 8d2a0000 1090021 112a0001 8000c0c 350b004f 3c094567 c000c07
  //   350c0062 800000f 2116821 2117021
endmodule

module GPR (
  input  WE_regwrite,
  input  [31:0] WD,
  input  clk,
  input  reset,
  input  [4:0] RA,
  input  [4:0] RB,
  input  [4:0] RW,
  input  jal_sel,
  output [31:0] RD1,
  output [31:0] RD2
);

  wire e0, e1, e2, e3, e4, e5, e6, e7, e8, e9, e10, e11, e12, e13, e14, e15, e16, e17, e18, e19, e20, e21,
       e22, e23, e24, e25, e26, e27, e28, e29, e30, e31;
  wire [4:0] multiplexer_1_out;
  wire [31:0] r0, r1, r2, r3, r4, r5, r6, r7, r8, r9, r10, r11, r12, r13, r14, r15, r16, r17, r18, r19, r20,
       r21, r22, r23, r24, r25, r26, r27, r28, r29, r30, r31;

  Decoder #(.select(5), .disabled(0)) decoder_1 (
    .out0(e0), .out1(e1), .out2(e2), .out3(e3), .out4(e4), .out5(e5), .out6(e6), .out7(e7), .out8(e8),
    .out9(e9), .out10(e10), .out11(e11), .out12(e12), .out13(e13), .out14(e14), .out15(e15), .out16(e16),
    .out17(e17), .out18(e18), .out19(e19), .out20(e20), .out21(e21), .out22(e22), .out23(e23), .out24(e24),
    .out25(e25), .out26(e26), .out27(e27), .out28(e28), .out29(e29), .out30(e30), .out31(e31),
    .sel(multiplexer_1_out), .en(WE_regwrite));
  Multiplexer #(.width(5), .disabled(0), .enable("false")) multiplexer_1 (
    .in0(RW), .in1({5{1'b1}}), .out(multiplexer_1_out), .sel(jal_sel));
  Register #(.width(32)) _0 (.D(WD), .en(1'b0), .Q(r0), .clk(clk), .clr(reset));
  Register #(.width(32)) _1 (.D(WD), .en(e1), .Q(r1), .clk(clk), .clr(reset));
  Register #(.width(32)) _2 (.D(WD), .en(e2), .Q(r2), .clk(clk), .clr(reset));
  Register #(.width(32)) _3 (.D(WD), .en(e3), .Q(r3), .clk(clk), .clr(reset));
  Register #(.width(32)) _4 (.D(WD), .en(e4), .Q(r4), .clk(clk), .clr(reset));
  Register #(.width(32)) _5 (.D(WD), .en(e5), .Q(r5), .clk(clk), .clr(reset));
  Register #(.width(32)) _6 (.D(WD), .en(e6), .Q(r6), .clk(clk), .clr(reset));
  Register #(.width(32)) _7 (.D(WD), .en(e7), .Q(r7), .clk(clk), .clr(reset));
  Multiplexer #(.select(5), .width(32), .enable("false")) multiplexer_2 (
    .in0(r0), .in1(r1), .in2(r2), .in3(r3), .in4(r4), .in5(r5), .in6(r6), .in7(r7), .in8(r8), .in9(r9),
    .in10(r10), .in11(r11), .in12(r12), .in13(r13), .in14(r14), .in15(r15), .in16(r16), .in17(r17),
    .in18(r18), .in19(r19), .in20(r20), .in21(r21), .in22(r22), .in23(r23), .in24(r24), .in25(r25),
    .in26(r26), .in27(r27), .in28(r28), .in29(r29), .in30(r30), .in31(r31), .out(RD1), .sel(RA));
  Register #(.width(32)) _8 (.D(WD), .en(e8), .Q(r8), .clk(clk), .clr(reset));
  Register #(.width(32)) _9 (.D(WD), .en(e9), .Q(r9), .clk(clk), .clr(reset));
  Register #(.width(32)) _10 (.D(WD), .en(e10), .Q(r10), .clk(clk), .clr(reset));
  Register #(.width(32)) _11 (.D(WD), .en(e11), .Q(r11), .clk(clk), .clr(reset));
  Register #(.width(32)) _12 (.D(WD), .en(e12), .Q(r12), .clk(clk), .clr(reset));
  Register #(.width(32)) _13 (.D(WD), .en(e13), .Q(r13), .clk(clk), .clr(reset));
  Register #(.width(32)) _14 (.D(WD), .en(e14), .Q(r14), .clk(clk), .clr(reset));
  Register #(.width(32)) _15 (.D(WD), .en(e15), .Q(r15), .clk(clk), .clr(reset));
  Register #(.width(32)) _16 (.D(WD), .en(e16), .Q(r16), .clk(clk), .clr(reset));
  Register #(.width(32)) _17 (.D(WD), .en(e17), .Q(r17), .clk(clk), .clr(reset));
  Register #(.width(32)) _18 (.D(WD), .en(e18), .Q(r18), .clk(clk), .clr(reset));
  Register #(.width(32)) _19 (.D(WD), .en(e19), .Q(r19), .clk(clk), .clr(reset));
  Register #(.width(32)) _20 (.D(WD), .en(e20), .Q(r20), .clk(clk), .clr(reset));
  Register #(.width(32)) _21 (.D(WD), .en(e21), .Q(r21), .clk(clk), .clr(reset));
  Register #(.width(32)) _22 (.D(WD), .en(e22), .Q(r22), .clk(clk), .clr(reset));
  Register #(.width(32)) _23 (.D(WD), .en(e23), .Q(r23), .clk(clk), .clr(reset));
  Multiplexer #(.select(5), .width(32), .enable("false")) multiplexer_3 (
    .in0(r0), .in1(r1), .in2(r2), .in3(r3), .in4(r4), .in5(r5), .in6(r6), .in7(r7), .in8(r8), .in9(r9),
    .in10(r10), .in11(r11), .in12(r12), .in13(r13), .in14(r14), .in15(r15), .in16(r16), .in17(r17),
    .in18(r18), .in19(r19), .in20(r20), .in21(r21), .in22(r22), .in23(r23), .in24(r24), .in25(r25),
    .in26(r26), .in27(r27), .in28(r28), .in29(r29), .in30(r30), .in31(r31), .out(RD2), .sel(RB));
  Register #(.width(32)) _24 (.D(WD), .en(e24), .Q(r24), .clk(clk), .clr(reset));
  Register #(.width(32)) _25 (.D(WD), .en(e25), .Q(r25), .clk(clk), .clr(reset));
  Register #(.width(32)) _26 (.D(WD), .en(e26), .Q(r26), .clk(clk), .clr(reset));
  Register #(.width(32)) _27 (.D(WD), .en(e27), .Q(r27), .clk(clk), .clr(reset));
  Register #(.width(32)) _28 (.D(WD), .en(e28), .Q(r28), .clk(clk), .clr(reset));
  Register #(.width(32)) _29 (.D(WD), .en(e29), .Q(r29), .clk(clk), .clr(reset));
  Register #(.width(32)) _30 (.D(WD), .en(e30), .Q(r30), .clk(clk), .clr(reset));
  Register #(.width(32)) _31 (.D(WD), .en(e31), .Q(r31), .clk(clk), .clr(reset));
endmodule

module ALU (
  input  [31:0] A,
  input  [31:0] B,
  input  [2:0] F,
  output [31:0] out,
  output zero
);

  wire [31:0] add32_1_s, or_1_out, sub32_1_s;

  add32 add32_1 (.a(A), .b(B), .s(add32_1_s));  // open: c
  sub32 sub32_1 (.a(A), .b(B), .s(sub32_1_s));
  assign or_1_out = A | B;  // OR_Gate or_1, 32 bits wide
  Multiplexer #(.select(3), .width(32), .enable("false")) multiplexer_1 (
    .in0(add32_1_s), .in1(sub32_1_s), .in2(or_1_out), .in3(B), .out(out), .sel(F));  // open: in4, in5, in6, in7
  Comparator #(.width(32)) comparator_1 (.a(out), .b({32{1'b0}}), .eq(zero));  // open: gt, lt
endmodule

module Controller (
  input  [5:0] opcode,
  input  [5:0] funct,
  output RegDst,
  output ALUSrc,
  output MemtoReg,
  output RegWrite,
  output MemWrite,
  output nPC_sel,
  output PC_j,
  output jal_sel,
  output [1:0] ExtOp,
  output [2:0] ALUCtr
);

  wire addu_out, j_out, not_1_out, not_2_out, not_3_out, not_4_out, not_5_out, not_6_out, not_7_out,
       not_8_out, not_9_out, not_10_out, not_11_out, not_12_out, ori_out, subu_out;

  not not_1 (not_1_out, opcode[5]);
  not not_2 (not_2_out, opcode[3]);
  not not_3 (not_3_out, opcode[4]);
  not not_4 (not_4_out, opcode[2]);
  not not_5 (not_5_out, opcode[0]);
  not not_6 (not_6_out, opcode[1]);
  not not_7 (not_7_out, funct[4]);
  not not_8 (not_8_out, funct[5]);
  not not_9 (not_9_out, funct[3]);
  not not_10 (not_10_out, funct[1]);
  not not_11 (not_11_out, funct[2]);
  not not_12 (not_12_out, funct[0]);
  and addu (addu_out, not_1_out, not_3_out, not_2_out, not_4_out, not_6_out, not_5_out, funct[5], not_7_out, not_9_out, not_11_out, not_10_out, funct[0]);
  and subu (subu_out, not_1_out, not_3_out, not_2_out, not_4_out, not_6_out, not_5_out, funct[5], not_7_out, not_9_out, not_11_out, funct[1], funct[0]);
  and ori (ori_out, not_1_out, not_3_out, opcode[3], opcode[2], not_6_out, opcode[0]);
  and lw (MemtoReg, opcode[5], not_3_out, not_2_out, not_4_out, opcode[1], opcode[0]);
  and sw (MemWrite, opcode[5], not_3_out, opcode[3], not_4_out, opcode[1], opcode[0]);
  and beq (nPC_sel, not_1_out, not_3_out, not_2_out, opcode[2], not_6_out, not_5_out);
  and j (j_out, not_1_out, not_3_out, not_2_out, not_4_out, opcode[1], not_5_out);
  and lui (ExtOp[1], not_1_out, not_3_out, opcode[3], opcode[2], opcode[1], opcode[0]);
  and jal (jal_sel, not_1_out, not_3_out, not_2_out, not_4_out, opcode[1], opcode[0]);
  or u_RegDst (RegDst, addu_out, subu_out);
  or u_ALUSrc (ALUSrc, ori_out, MemtoReg, MemWrite, ExtOp[1]);
  or u_RegWrite (RegWrite, ExtOp[1], addu_out, subu_out, ori_out, MemtoReg, jal_sel);
  or u_ExtOp (ExtOp[0], MemtoReg, MemWrite);
  or ALUCtr_2 (ALUCtr[2], 1'b0, 1'b0);
  or ALUCtr_1 (ALUCtr[1], ori_out, ExtOp[1]);
  or ALUCtr_0 (ALUCtr[0], subu_out, ExtOp[1], nPC_sel);
  or u_PC_j (PC_j, j_out, jal_sel);
endmodule

module Extender (
  input  [15:0] Imm16,
  input  [1:0] Extsel,
  output [31:0] ExtImm32
);

  wire [31:0] bit_extender_1_out, bit_extender_2_out, shifter_1_out;

  assign bit_extender_1_out = {{16{1'b0}}, Imm16};  // Bit_Extender bit_extender_1
  Shifter #(.width(32)) shifter_1 (.in(bit_extender_1_out), .\dist (5'b10000), .out(shifter_1_out));
  assign bit_extender_2_out = {{16{Imm16[15]}}, Imm16};  // Bit_Extender bit_extender_2
  Multiplexer #(.select(2), .width(32), .disabled(0), .enable("false")) multiplexer_1 (
    .in0(bit_extender_1_out), .in1(bit_extender_2_out), .in2(shifter_1_out), .out(ExtImm32), .sel(Extsel));  // open: in3
endmodule

module DM (
  input  [4:0] A,
  input  [31:0] D,
  input  MemWrite,
  input  reset,
  input  clk,
  input  MemtoReg,
  output [31:0] dmout
);

  RAM #(.addrWidth(5), .dataWidth(32), .bus("separate")) ram_1 (
    .addr(A), .din(D), .data(dmout), .str(MemWrite), .sel(1'b1), .clk(clk), .ld(MemtoReg), .clr(reset));
endmodule

// add
module add1 (
  input  a,
  input  b,
  input  c0,
  output s,
  output c
);

  wire and_1_out, and_2_out, xor_1_out;

  xor xor_1 (xor_1_out, a, b);
  and and_1 (and_1_out, b, a);
  xor xor_2 (s, xor_1_out, c0);
  and and_2 (and_2_out, xor_1_out, c0);
  or or_1 (c, and_2_out, and_1_out);
endmodule

// add
module add8 (
  input  [7:0] a,
  input  [7:0] b,
  input  c0,
  output c7,
  output [7:0] s
);

  wire add1_1_c, add1_2_c, add1_3_c, add1_4_c, add1_5_c, add1_6_c, add1_7_c;

  add1 add1_1 (.a(a[0]), .b(b[0]), .c0(c0), .s(s[0]), .c(add1_1_c));
  add1 add1_2 (.a(a[1]), .b(b[1]), .c0(add1_1_c), .s(s[1]), .c(add1_2_c));
  add1 add1_3 (.a(a[2]), .b(b[2]), .c0(add1_2_c), .s(s[2]), .c(add1_3_c));
  add1 add1_4 (.a(a[3]), .b(b[3]), .c0(add1_3_c), .s(s[3]), .c(add1_4_c));
  add1 add1_5 (.a(a[4]), .b(b[4]), .c0(add1_4_c), .s(s[4]), .c(add1_5_c));
  add1 add1_6 (.a(a[5]), .b(b[5]), .c0(add1_5_c), .s(s[5]), .c(add1_6_c));
  add1 add1_7 (.a(a[6]), .b(b[6]), .c0(add1_6_c), .s(s[6]), .c(add1_7_c));
  add1 add1_8 (.a(a[7]), .b(b[7]), .c0(add1_7_c), .s(s[7]), .c(c7));
endmodule

module add32 (
  input  [31:0] a,
  input  [31:0] b,
  output c,
  output [31:0] s
);

  wire add8_1_c7, add8_2_c7, add8_3_c7;

  add8 add8_1 (.c0(1'b0), .a(a[7:0]), .b(b[7:0]), .s(s[7:0]), .c7(add8_1_c7));
  add8 add8_2 (.c0(add8_1_c7), .a(a[15:8]), .b(b[15:8]), .s(s[15:8]), .c7(add8_2_c7));
  add8 add8_3 (.c0(add8_2_c7), .a(a[23:16]), .b(b[23:16]), .s(s[23:16]), .c7(add8_3_c7));
  add8 add8_4 (.c0(add8_3_c7), .a(a[31:24]), .b(b[31:24]), .s(s[31:24]), .c7(c));
endmodule

module sub32 (
  input  [31:0] a,
  input  [31:0] b,
  output [31:0] s
);

  wire [31:0] add32_1_s, not_1_out;

  assign not_1_out = ~b;  // NOT_Gate not_1, 32 bits wide
  add32 add32_1 (.a(not_1_out), .b(32'h1), .s(add32_1_s));  // open: c
  add32 add32_2 (.a(a), .b(add32_1_s), .s(s));  // open: c
endmodule
